// Logisim project MIPS16.circ as structural Verilog: 4 circuits, main circuit main
module main (
  input  RST,
  output [1:0] func
);

  wire alu_1_zero, and_1_out, and_2_out, clock_1_out, control_1_alop, control_1_alop_i, control_1_beq,
       control_1_bne, control_1_lw, control_1_sw, not_1_out, or_1_out, or_2_out, or_3_out, or_4_out, or_5_out;
  wire [1:0] multiplexer_4_out, multiplexer_5_out;
  wire [2:0] control_1_rd, control_1_rs, control_1_rt, multiplexer_3_out;
  wire [4:0] control_1_val;
  wire [7:0] adder_1_out, bit_extender_1_out, multiplexer_1_out, PC_q;
  wire [15:0] alu_1_result, DATA_MEM_dout, INSTR_MEM_data, multiplexer_2_out, multiplexer_6_out,
       registers_1_r1, registers_1_r2, registers_1_r3, registers_1_r4, registers_1_r5, registers_1_r6,
       registers_1_r7, registers_1_read_data_1, registers_1_read_data_2;

  Multiplexer #(.enable("false"), .width(8)) multiplexer_1 (
    .in0(8'h1), .in1(bit_extender_1_out), .out(multiplexer_1_out), .sel(or_1_out));
  Adder adder_1 (.a(PC_q), .b(multiplexer_1_out), .out(adder_1_out));  // open: cin, cout
  Clock clock_1 (.out(clock_1_out));
  Register PC (.D(adder_1_out), .en(1'b1), .clk(clock_1_out), .Q(PC_q), .clr(RST));
  ROM #(.dataWidth(16)) INSTR_MEM (.addr(PC_q), .data(INSTR_MEM_data));
  or or_1 (or_1_out, and_1_out, and_2_out);
  and and_1 (and_1_out, alu_1_zero, control_1_beq);
  and and_2 (and_2_out, not_1_out, control_1_bne);
  assign bit_extender_1_out = {{3{control_1_val[4]}}, control_1_val};  // Bit_Extender bit_extender_1
  control control_1 (
    .Instr(INSTR_MEM_data), .ALOP(control_1_alop), .BEQ(control_1_beq), .BNE(control_1_bne),
    .ALOP_I(control_1_alop_i), .LW(control_1_lw), .SW(control_1_sw), .FUNC(func), .RS(control_1_rs),
    .RT(control_1_rt), .RD(control_1_rd), .VAL(control_1_val));
  not not_1 (not_1_out, alu_1_zero);
  or or_2 (or_2_out, control_1_alop, control_1_alop_i, control_1_lw);
  Multiplexer #(.enable("false"), .width(16)) multiplexer_2 (
    .in0({{11{1'b0}}, control_1_val}), .in1(registers_1_read_data_2), .out(multiplexer_2_out), .sel(or_3_out));
  or or_3 (or_3_out, control_1_alop, or_4_out);
  or or_4 (or_4_out, control_1_beq, control_1_bne);
  ALU alu_1 (
    .OP1(registers_1_read_data_1), .OP2(multiplexer_2_out), .FUNC(multiplexer_4_out), .ZERO(alu_1_zero),
    .RESULT(alu_1_result));
  Multiplexer #(.enable("false"), .width(3)) multiplexer_3 (
    .in0(control_1_rt), .in1(control_1_rd), .out(multiplexer_3_out), .sel(control_1_alop));
  Hex_Digit_Display hex_digit_display_1 (.value(registers_1_read_data_1[15:12]));  // open: dp
  or or_5 (or_5_out, control_1_lw, control_1_sw);
  Hex_Digit_Display hex_digit_display_2 (.value(registers_1_read_data_1[11:8]));  // open: dp
  Hex_Digit_Display hex_digit_display_3 (.value(registers_1_read_data_1[7:4]));  // open: dp
  Multiplexer #(.enable("false"), .width(2)) multiplexer_4 (
    .in0(multiplexer_5_out), .in1(2'b01), .out(multiplexer_4_out), .sel(or_4_out));
  Multiplexer #(.enable("false"), .width(2)) multiplexer_5 (
    .in0(func), .in1(2'b00), .out(multiplexer_5_out), .sel(or_5_out));
  registers registers_1 (
    .READ_ADDR_1(control_1_rs), .READ_ADDR_2(control_1_rt), .WE(or_2_out), .WRITE_ADDR(multiplexer_3_out),
    .WRITE_DATA(multiplexer_6_out), .CLK(clock_1_out), .RST(RST), .READ_DATA_1(registers_1_read_data_1),
    .READ_DATA_2(registers_1_read_data_2), .R1(registers_1_r1), .R2(registers_1_r2), .R3(registers_1_r3),
    .R4(registers_1_r4), .R5(registers_1_r5), .R6(registers_1_r6), .R7(registers_1_r7));
  Hex_Digit_Display hex_digit_display_4 (.value(registers_1_read_data_1[3:0]));  // open: dp
  Hex_Digit_Display hex_digit_display_5 (.value(multiplexer_2_out[15:12]));  // open: dp
  Hex_Digit_Display hex_digit_display_6 (.value(registers_1_r1[15:12]));  // open: dp
  Hex_Digit_Display hex_digit_display_7 (.value(multiplexer_2_out[11:8]));  // open: dp
  Hex_Digit_Display hex_digit_display_8 (.value(multiplexer_2_out[7:4]));  // open: dp
  Hex_Digit_Display hex_digit_display_9 (.value(registers_1_r1[11:8]));  // open: dp
  Hex_Digit_Display hex_digit_display_10 (.value(registers_1_r1[7:4]));  // open: dp
  Hex_Digit_Display hex_digit_display_11 (.value(multiplexer_2_out[3:0]));  // open: dp
  Hex_Digit_Display hex_digit_display_12 (.value(registers_1_r1[3:0]));  // open: dp
  RAM #(.addrWidth(16), .asyncread("true"), .dataWidth(16)) DATA_MEM (
    .addr(alu_1_result), .we(control_1_sw), .oe(control_1_lw), .clk(clock_1_out),
    .din(registers_1_read_data_2), .dout(DATA_MEM_dout));
  Hex_Digit_Display hex_digit_display_13 (.value(registers_1_r2[15:12]));  // open: dp
  Hex_Digit_Display hex_digit_display_14 (.value(registers_1_r2[11:8]));  // open: dp
  Hex_Digit_Display hex_digit_display_15 (.value(registers_1_r2[7:4]));  // open: dp
  Hex_Digit_Display hex_digit_display_16 (.value(registers_1_r2[3:0]));  // open: dp
  Hex_Digit_Display hex_digit_display_17 (.value(registers_1_read_data_1[15:12]));  // open: dp
  Hex_Digit_Display hex_digit_display_18 (.value(registers_1_read_data_1[11:8]));  // open: dp
  Hex_Digit_Display hex_digit_display_19 (.value(registers_1_read_data_2[15:12]));  // open: dp
  Hex_Digit_Display hex_digit_display_20 (.value(registers_1_read_data_2[11:8]));  // open: dp
  Hex_Digit_Display hex_digit_display_21 (.value(registers_1_r3[15:12]));  // open: dp
  Hex_Digit_Display hex_digit_display_22 (.value(registers_1_r3[11:8]));  // open: dp
  Hex_Digit_Display hex_digit_display_23 (.value(registers_1_read_data_1[7:4]));  // open: dp
  Hex_Digit_Display hex_digit_display_24 (.value(registers_1_read_data_1[3:0]));  // open: dp
  Hex_Digit_Display hex_digit_display_25 (.value(registers_1_read_data_2[7:4]));  // open: dp
  Hex_Digit_Display hex_digit_display_26 (.value(registers_1_read_data_2[3:0]));  // open: dp
  Hex_Digit_Display hex_digit_display_27 (.value(registers_1_r3[7:4]));  // open: dp
  Hex_Digit_Display hex_digit_display_28 (.value(registers_1_r3[3:0]));  // open: dp
  Multiplexer #(.enable("false"), .width(16)) multiplexer_6 (
    .in0(alu_1_result), .in1(DATA_MEM_dout), .out(multiplexer_6_out), .sel(control_1_lw));
  Hex_Digit_Display hex_digit_display_29 (.value(registers_1_r4[15:12]));  // open: dp
  Hex_Digit_Display hex_digit_display_30 (.value(registers_1_r4[11:8]));  // open: dp
  Hex_Digit_Display hex_digit_display_31 (.value(alu_1_result[15:12]));  // open: dp
  Hex_Digit_Display hex_digit_display_32 (.value(DATA_MEM_dout[15:12]));  // open: dp
  Hex_Digit_Display hex_digit_display_33 (.value(registers_1_r4[7:4]));  // open: dp
  Hex_Digit_Display hex_digit_display_34 (.value(registers_1_r4[3:0]));  // open: dp
  Hex_Digit_Display hex_digit_display_35 (.value(alu_1_result[11:8]));  // open: dp
  Hex_Digit_Display hex_digit_display_36 (.value(alu_1_result[7:4]));  // open: dp
  Hex_Digit_Display hex_digit_display_37 (.value(DATA_MEM_dout[11:8]));  // open: dp
  Hex_Digit_Display hex_digit_display_38 (.value(DATA_MEM_dout[7:4]));  // open: dp
  Hex_Digit_Display hex_digit_display_39 (.value(multiplexer_6_out[15:12]));  // open: dp
  Hex_Digit_Display hex_digit_display_40 (.value(multiplexer_6_out[11:8]));  // open: dp
  Hex_Digit_Display hex_digit_display_41 (.value(registers_1_r5[15:12]));  // open: dp
  Hex_Digit_Display hex_digit_display_42 (.value(alu_1_result[3:0]));  // open: dp
  Hex_Digit_Display hex_digit_display_43 (.value(DATA_MEM_dout[3:0]));  // open: dp
  Hex_Digit_Display hex_digit_display_44 (.value(multiplexer_6_out[7:4]));  // open: dp
  Hex_Digit_Display hex_digit_display_45 (.value(multiplexer_6_out[3:0]));  // open: dp
  Hex_Digit_Display hex_digit_display_46 (.value(registers_1_r5[11:8]));  // open: dp
  Hex_Digit_Display hex_digit_display_47 (.value(registers_1_r5[7:4]));  // open: dp
  Hex_Digit_Display hex_digit_display_48 (.value(registers_1_r5[3:0]));  // open: dp
  Hex_Digit_Display hex_digit_display_49 (.value(registers_1_r6[15:12]));  // open: dp
  Hex_Digit_Display hex_digit_display_50 (.value(registers_1_r6[11:8]));  // open: dp
  Hex_Digit_Display hex_digit_display_51 (.value(registers_1_r6[7:4]));  // open: dp
  Hex_Digit_Display hex_digit_display_52 (.value(registers_1_r6[3:0]));  // open: dp
  Hex_Digit_Display hex_digit_display_53 (.value(registers_1_r7[15:12]));  // open: dp
  Hex_Digit_Display hex_digit_display_54 (.value(registers_1_r7[11:8]));  // open: dp
  Hex_Digit_Display hex_digit_display_55 (.value(registers_1_r7[7:4]));  // open: dp
  Hex_Digit_Display hex_digit_display_56 (.value(registers_1_r7[3:0]));  // open: dp

  // Notes on the sheet:
  //   branch offset
  //   branch condition
  //   contents of INSTR_MEM (hex, n*v repeats v):
  //   a12a a7ef a921 534 89e0 491d 8da0 8520 8820
  //   Memory address
  //   branch condition
  //   extend sign
  //   ZERO and BEQ
  //   not ZERO and BNE
  //   Instruction
  //   RS
  //   extend VAL
  //   RT
  //   ALU_FUNC
  //   WE_REG=ALOP or ALOP_I or LW
  //   ALOP
  //   RS
  //   ALOP or BEQ or BNE
  //   BEQ or BNE
  //   RST
  //   OP2 = RT if (ALOP or BEQ or BNE )else VAL
  //   CLK
  //   OP1
  //   LW OR SW
  //   LW
  //   WRITE_ADDR = RD if ALOP else RT
  //   FUNC
  //   subtraction
  //   addition
  //   q(RS)
  //   q(RT)
  //   OP2
  //   ALU_FUNC = ADD if (LW or SW) else SUB if (BNE or BEQ) else FUNC
  //   LW
  //   SW
  //   R1
  //   ADDR
  //   DATA_in
  //   R2
  //   RS
  //   RT
  //   R3
  //   DATA_out
  //   R4
  //   ADDR
  //   write_data
  //   write_data = RAM_out if LW else ALU_RESULT
  //   write_data
  //   R5
  //   R6
  //   R7
endmodule

module control (
  input  [15:0] Instr,
  output ALOP,
  output BEQ,
  output BNE,
  output ALOP_I,
  output LW,
  output SW,
  output [1:0] FUNC,
  output [2:0] RS,
  output [2:0] RT,
  output [2:0] RD,
  output [4:0] VAL
);

  wire and_2_out, not_1_out, not_2_out, not_3_out, not_4_out, not_5_out;

  not not_1 (not_1_out, Instr[11]);
  not not_2 (not_2_out, Instr[12]);
  not not_3 (not_3_out, Instr[15]);
  not not_4 (not_4_out, Instr[14]);
  not not_5 (not_5_out, Instr[13]);
  and and_1 (ALOP, not_3_out, not_4_out, not_5_out);
  and and_2 (and_2_out, not_3_out, Instr[14], not_5_out);
  and and_3 (ALOP_I, Instr[15], not_4_out, Instr[13]);
  and and_4 (LW, Instr[15], not_4_out, not_5_out, not_2_out, not_1_out);
  and and_5 (SW, Instr[15], not_4_out, not_5_out, not_2_out, Instr[11]);
  and and_6 (BEQ, not_2_out, not_1_out, and_2_out);
  and and_7 (BNE, and_2_out, not_2_out, Instr[11]);

  assign FUNC = Instr[12:11];
  assign RD = Instr[4:2];
  assign RS = Instr[10:8];
  assign RT = Instr[7:5];
  assign VAL = Instr[4:0];

  // Notes on the sheet:
  //   op_code
  //   RS
  //   RT
  //   instruction
  //   I(12)
  //   I(11)
  //   I(15)
  //   I(14)
  //   I(13)
  //   I(15)
  //   I(14)
  //   I(13)
  //   I(12)
  //   I(11)
  //   ADD, SUB, AND, OR
  //   BRANCH
  //   ADDI, SUBI
  //   LW
  //   SW
  //   RD
  //   value
  //   arith_op
  //   arithemtic-logic operation (R format)
  //   arithemtic-logic operation (immediate)
endmodule

module registers (
  input  [2:0] READ_ADDR_1,
  input  [2:0] READ_ADDR_2,
  input  WE,
  input  [2:0] WRITE_ADDR,
  input  [15:0] WRITE_DATA,
  input  CLK,
  input  RST,
  output [15:0] READ_DATA_1,
  output [15:0] READ_DATA_2,
  output [15:0] R1,
  output [15:0] R2,
  output [15:0] R3,
  output [15:0] R4,
  output [15:0] R5,
  output [15:0] R6,
  output [15:0] R7
);

  wire decoder_1_out1, decoder_1_out2, decoder_1_out3, decoder_1_out4, decoder_1_out5, decoder_1_out6,
       decoder_1_out7;
  wire [15:0] REG0_q;

  Decoder #(.select(3)) decoder_1 (
    .out1(decoder_1_out1), .out2(decoder_1_out2), .out3(decoder_1_out3), .out4(decoder_1_out4),
    .out5(decoder_1_out5), .out6(decoder_1_out6), .out7(decoder_1_out7), .sel(WRITE_ADDR), .en(WE));  // open: out0
  Register #(.width(16)) REG0 (.en(1'b0), .clk(CLK), .Q(REG0_q), .clr(RST));  // open: D
  Register #(.width(16)) REG1 (.D(WRITE_DATA), .en(decoder_1_out1), .clk(CLK), .Q(R1), .clr(RST));
  Register #(.width(16)) REG2 (.D(WRITE_DATA), .en(decoder_1_out2), .clk(CLK), .Q(R2), .clr(RST));
  Register #(.width(16)) REG3 (.D(WRITE_DATA), .en(decoder_1_out3), .clk(CLK), .Q(R3), .clr(RST));
  Register #(.width(16)) REG4 (.D(WRITE_DATA), .en(decoder_1_out4), .clk(CLK), .Q(R4), .clr(RST));
  Register #(.width(16)) REG5 (.D(WRITE_DATA), .en(decoder_1_out5), .clk(CLK), .Q(R5), .clr(RST));
  Register #(.width(16)) REG6 (.D(WRITE_DATA), .en(decoder_1_out6), .clk(CLK), .Q(R6), .clr(RST));
  Register #(.width(16)) REG7 (.D(WRITE_DATA), .en(decoder_1_out7), .clk(CLK), .Q(R7), .clr(RST));
  Multiplexer #(.enable("false"), .select(3), .width(16)) multiplexer_1 (
    .in0(REG0_q), .in1(R1), .in2(R2), .in3(R3), .in4(R4), .in5(R5), .in6(R6), .in7(R7), .out(READ_DATA_1),
    .sel(READ_ADDR_1));
  Multiplexer #(.enable("false"), .select(3), .width(16)) multiplexer_2 (
    .in0(REG0_q), .in1(R1), .in2(R2), .in3(R3), .in4(R4), .in5(R5), .in6(R6), .in7(R7), .out(READ_DATA_2),
    .sel(READ_ADDR_2));
endmodule

module ALU (
  input  [15:0] OP1,
  input  [15:0] OP2,
  input  [1:0] FUNC,
  output ZERO,
  output [15:0] RESULT
);

  wire [15:0] adder_1_out, and_1_out, or_1_out, subtractor_1_out;

  Adder #(.width(16)) adder_1 (.a(OP1), .b(OP2), .out(adder_1_out));  // open: cin, cout
  Subtractor #(.width(16)) subtractor_1 (.a(OP1), .b(OP2), .out(subtractor_1_out));  // open: bin, bout
  assign and_1_out = OP1 & OP2;  // AND_Gate and_1, 16 bits wide
  assign or_1_out = OP1 | OP2;  // OR_Gate or_1, 16 bits wide
  Multiplexer #(.enable("false"), .select(2), .width(16)) multiplexer_1 (
    .in0(adder_1_out), .in1(subtractor_1_out), .in2(and_1_out), .in3(or_1_out), .out(RESULT), .sel(FUNC));
  Comparator #(.width(16)) comparator_1 (.a({16{1'b0}}), .b(RESULT), .eq(ZERO));  // open: gt, lt
endmodule
